// Logisim project Compu.circ as structural Verilog
module main (
  output [7:0] out_1,
  output [7:0] out_2
);

  wire and_1_out, and_2_out, and_3_out, and_5_out, and_6_out, and_7_out, and_8_out, and_9_out, and_10_out,
       and_11_out, and_12_out, BufferInScreen_q, clock_1_out, comparator_1_eq, comparator_2_eq,
       comparator_3_eq, comparator_3_lt, comparator_4_eq, counter_2_q, counter_3_q, d_ff_1_q, d_ff_2_q,
       d_ff_3_q, d_ff_4_q, d_ff_5_q, d_ff_6_q, d_ff_7_q, d_ff_8_q, d_ff_9_q, demultiplexer_1_out0,
       demultiplexer_1_out1, demultiplexer_2_out1, demultiplexer_2_out2, demultiplexer_2_out3,
       demultiplexer_2_out4, demultiplexer_2_out5, demultiplexer_2_out6, demultiplexer_2_out7,
       demultiplexer_2_out8, demultiplexer_2_out9, demultiplexer_2_out10, demultiplexer_2_out11,
       demultiplexer_2_out12, demultiplexer_2_out13, demultiplexer_3_out0, demultiplexer_3_out1, not_1_out,
       not_2_out, not_3_out, not_5_out, not_6_out, not_7_out, not_8_out, not_9_out, not_10_out, or_1_out,
       or_2_out, or_3_out, or_5_out, or_6_out, or_7_out, or_8_out, or_9_out, or_10_out, or_11_out,
       ram_load_read_controller_1_load, ram_load_read_controller_1_store, ram_load_read_controller_2_load,
       ram_load_read_controller_2_store, ram_load_read_controller_3_load, ram_load_read_controller_3_store,
       ram_load_read_controller_4_load, ram_load_read_controller_4_store, ram_load_read_controller_5_load,
       ram_load_read_controller_5_store, RESET_out, s_r_ff_1_q;
  wire [2:0] IR_q_2;
  wire [5:0] counter_4_q, divider_2_out, divider_2_rem;
  wire [7:0] IR_q;
  wire [10:0] counter_1_q, multiplexer_1_out, multiplexer_4_out, PC_1_q;
  wire [13:0] ADR_CACHE_q, multiplexer_5_out;
  wire [15:0] adder_3_out, multiplexer_9_out, multiplexer_10_out, SCREEN_q;
  wire [23:0] adder_1_out, adder_2_out, and_4_out, bit_extender_5_out, demultiplexer_4_out0,
       demultiplexer_4_out1, divider_1_out, divider_1_rem, FrameBuffer0_dout, FrameBuffer1_dout,
       multiplexer_2_out, multiplier_1_cout, multiplier_1_out, not_4_out, or_4_out, Resources_data,
       rgb_video_1_p6, subtractor_1_out, xor_1_out;
  wire [28:0] multiplexer_7_out, multiplexer_8_out, PC_1_q_2, register_1_q, register_2_q;
  wire [39:0] PC_0_q;
  wire [47:0] bit_extender_1_out, bit_extender_2_out, GPU_INST_q, multiplexer_3_out;
  wire [47:14] multiplexer_5_out_2;
  wire [51:0] bit_extender_3_out, bit_extender_4_out, CACHE_L2_dout, COMPLEX_ALU_DATA_q, IR_q_3, R0_q, R1_q,
       R2_q, R3_q, SIMPLE_ALU_DATA_q;
  wire [51:48] multiplexer_5_out_3;
  wire [59:0] multiplexer_6_out, ram_1_dout, ram_2_dout, rom_1_data;

  or or_1 (or_1_out, demultiplexer_2_out13, and_8_out, d_ff_1_q);
  D_Flip_Flop d_ff_1 (.clk(clock_1_out), .D(or_1_out), .Q(d_ff_1_q), .reset(or_3_out));  // open: Qn, preset
  not not_1 (not_1_out, d_ff_1_q);
  or or_2 (or_2_out, and_3_out, demultiplexer_2_out13);
  or or_3 (or_3_out, d_ff_4_q, and_3_out);
  Clock clock_1 (.out(clock_1_out));
  Button RESET (.out(RESET_out));
  Counter #(.max('h7ff), .width(11)) counter_1 (
    .count(d_ff_1_q), .Q(counter_1_q), .up(1'b1), .clk(clock_1_out), .clr(or_2_out));  // open: load, D, carry
  and and_1 (and_1_out, not_1_out, d_ff_8_q);
  ROM #(.addrWidth(11), .dataWidth(60)) rom_1 (.addr(counter_1_q), .data(rom_1_data));
  Register #(.width(52)) SIMPLE_ALU_DATA (
    .D({multiplexer_5_out_3, multiplexer_5_out_2, multiplexer_5_out}), .en(demultiplexer_2_out1),
    .clk(clock_1_out), .Q(SIMPLE_ALU_DATA_q), .clr(and_3_out));
  Register #(.width(52)) COMPLEX_ALU_DATA (
    .D({multiplexer_5_out_3, multiplexer_5_out_2, multiplexer_5_out}), .en(demultiplexer_2_out2),
    .clk(clock_1_out), .Q(COMPLEX_ALU_DATA_q), .clr(and_3_out));
  D_Flip_Flop d_ff_2 (.clk(clock_1_out), .D(and_1_out), .Q(d_ff_2_q));  // open: Qn, preset, reset
  Demultiplexer demultiplexer_1 (
    .out0(demultiplexer_1_out0), .out1(demultiplexer_1_out1), .in(demultiplexer_3_out1), .sel(or_5_out));
  not not_2 (not_2_out, d_ff_3_q);
  D_Flip_Flop d_ff_3 (.clk(clock_1_out), .D(RESET_out), .Q(d_ff_3_q));  // open: Qn, preset, reset
  D_Flip_Flop d_ff_4 (.clk(clock_1_out), .D(comparator_1_eq), .Q(d_ff_4_q));  // open: Qn, preset, reset
  Comparator #(.mode("unsigned"), .width(11)) comparator_1 (
    .a(counter_1_q), .b({11{1'b1}}), .eq(comparator_1_eq));  // open: gt, lt
  not not_3 (not_3_out, d_ff_2_q);
  and and_2 (and_2_out, not_3_out, and_1_out);
  Counter #(.max('hffffffffff), .width(40)) PC_0 (
    .load(demultiplexer_2_out10), .D({multiplexer_5_out_2[39:14], multiplexer_5_out}),
    .count(demultiplexer_1_out0), .Q(PC_0_q), .up(1'b1), .clk(clock_1_out), .clr(and_3_out));  // open: carry
  and and_3 (and_3_out, not_2_out, RESET_out);
  Counter #(.max('h1), .width(1)) counter_2 (
    .count(and_2_out), .Q(counter_2_q), .up(1'b1), .clk(clock_1_out), .clr(and_3_out));  // open: load, D, carry
  Adder #(.width(24)) adder_1 (
    .a(SIMPLE_ALU_DATA_q[23:0]), .b(SIMPLE_ALU_DATA_q[47:24]), .out(adder_1_out));  // open: cin, cout
  Subtractor #(.width(24)) subtractor_1 (
    .a(SIMPLE_ALU_DATA_q[23:0]), .b(SIMPLE_ALU_DATA_q[47:24]), .out(subtractor_1_out));  // open: bin, bout
  assign and_4_out = SIMPLE_ALU_DATA_q[23:0] & SIMPLE_ALU_DATA_q[47:24];  // AND_Gate and_4, 24 bits wide
  assign or_4_out = SIMPLE_ALU_DATA_q[23:0] | SIMPLE_ALU_DATA_q[47:24];  // OR_Gate or_4, 24 bits wide
  assign xor_1_out = SIMPLE_ALU_DATA_q[23:0] ^ SIMPLE_ALU_DATA_q[47:24];  // XOR_Gate xor_1, 24 bits wide
  assign not_4_out = ~SIMPLE_ALU_DATA_q[23:0];  // NOT_Gate not_4, 24 bits wide
  Multiplier #(.mode("twosComplement"), .width(24)) multiplier_1 (
    .a(COMPLEX_ALU_DATA_q[23:0]), .b(COMPLEX_ALU_DATA_q[47:24]), .out(multiplier_1_out),
    .cout(multiplier_1_cout));  // open: cin
  assign bit_extender_1_out = {{24{1'b0}}, divider_1_out};  // Bit_Extender bit_extender_1
  Divider #(.mode("twosComplement"), .width(24)) divider_1 (
    .a(COMPLEX_ALU_DATA_q[23:0]), .b(COMPLEX_ALU_DATA_q[47:24]), .out(divider_1_out), .rem(divider_1_rem));  // open: upper
  assign bit_extender_2_out = {{24{1'b0}}, divider_1_rem};  // Bit_Extender bit_extender_2
  Counter #(.max('hffffffffff), .width(40)) PC_1 (
    .load(demultiplexer_2_out11), .D({multiplexer_5_out_2[39:14], multiplexer_5_out}),
    .count(demultiplexer_1_out1), .Q({PC_1_q_2, PC_1_q}), .up(1'b1), .clk(clock_1_out), .clr(and_3_out));  // open: carry
  Multiplexer #(.width(11)) multiplexer_1 (.in0(PC_1_q), .in1(counter_1_q), .out(multiplexer_1_out), .sel(not_5_out));
  or or_5 (or_5_out, counter_2_q, d_ff_5_q);
  not not_5 (not_5_out, or_5_out);
  Multiplexer #(.select(3), .width(24)) multiplexer_2 (
    .in0(adder_1_out), .in1(subtractor_1_out), .in2(and_4_out), .in3(or_4_out), .in4(xor_1_out),
    .in5(not_4_out), .out(multiplexer_2_out), .sel(SIMPLE_ALU_DATA_q[51:49]));  // open: in6, in7
  Multiplexer #(.select(2), .width(48)) multiplexer_3 (
    .in0({multiplier_1_cout, multiplier_1_out}), .in1(bit_extender_1_out), .in2(bit_extender_2_out),
    .out(multiplexer_3_out), .sel(COMPLEX_ALU_DATA_q[49:48]));  // open: in3
  RAM #(.addrWidth(11), .clearpin("true"), .dataWidth(60)) ram_1 (
    .addr(multiplexer_4_out), .we(ram_load_read_controller_1_store), .oe(ram_load_read_controller_1_load),
    .clk(clock_1_out), .din(rom_1_data), .dout(ram_1_dout), .clr(and_3_out));
  Multiplexer #(.width(11)) multiplexer_4 (
    .in0(PC_0_q[10:0]), .in1(counter_1_q), .out(multiplexer_4_out), .sel(or_5_out));
  RAM_LOAD_READ_CONTROLLER ram_load_read_controller_1 (
    .STORE_SIGNAL(or_5_out), .STORE(ram_load_read_controller_1_store), .LOAD(ram_load_read_controller_1_load));
  RAM #(.addrWidth(11), .clearpin("true"), .dataWidth(60)) ram_2 (
    .addr(multiplexer_1_out), .we(ram_load_read_controller_2_store), .oe(ram_load_read_controller_2_load),
    .clk(clock_1_out), .din(rom_1_data), .dout(ram_2_dout), .clr(and_3_out));
  RAM_LOAD_READ_CONTROLLER ram_load_read_controller_2 (
    .STORE_SIGNAL(not_5_out), .STORE(ram_load_read_controller_2_store), .LOAD(ram_load_read_controller_2_load));
  assign bit_extender_3_out = {{28{1'b0}}, multiplexer_2_out};  // Bit_Extender bit_extender_3
  assign bit_extender_4_out = {{4{1'b0}}, multiplexer_3_out};  // Bit_Extender bit_extender_4
  Demultiplexer #(.select(4)) demultiplexer_2 (
    .out1(demultiplexer_2_out1), .out2(demultiplexer_2_out2), .out3(demultiplexer_2_out3),
    .out4(demultiplexer_2_out4), .out5(demultiplexer_2_out5), .out6(demultiplexer_2_out6),
    .out7(demultiplexer_2_out7), .out8(demultiplexer_2_out8), .out9(demultiplexer_2_out9),
    .out10(demultiplexer_2_out10), .out11(demultiplexer_2_out11), .out12(demultiplexer_2_out12),
    .out13(demultiplexer_2_out13), .in(1'b1), .sel(IR_q[3:0]));  // open: out0, out14, out15
  Register #(.width(29)) register_1 (
    .D({multiplexer_5_out_2[28:14], multiplexer_5_out}), .en(or_5_out), .Q(register_1_q), .clk(clock_1_out),
    .clr(and_3_out));
  Register #(.width(29)) register_2 (
    .D({multiplexer_5_out_2[28:14], multiplexer_5_out}), .en(not_5_out), .Q(register_2_q), .clk(clock_1_out),
    .clr(and_3_out));
  Register #(.width(52)) R0 (
    .D({multiplexer_5_out_3, multiplexer_5_out_2, multiplexer_5_out}), .en(demultiplexer_2_out3),
    .clk(clock_1_out), .Q(R0_q), .clr(and_3_out));
  Multiplexer #(.select(3), .width(52)) multiplexer_5 (
    .in0(bit_extender_3_out), .in1(bit_extender_4_out), .in2(R0_q), .in3(R1_q), .in4(R2_q), .in5(R3_q),
    .in6(IR_q_3), .in7(CACHE_L2_dout), .out({multiplexer_5_out_3, multiplexer_5_out_2, multiplexer_5_out}),
    .sel(IR_q_2));
  Multiplexer #(.width(60)) multiplexer_6 (.in0(ram_1_dout), .in1(ram_2_dout), .out(multiplexer_6_out), .sel(or_5_out));
  Multiplexer #(.width(29)) multiplexer_7 (
    .in0(register_1_q), .in1(register_2_q), .out(multiplexer_7_out), .sel(or_5_out));
  Multiplexer #(.width(29)) multiplexer_8 (
    .in0(PC_0_q[39:11]), .in1(PC_1_q_2), .out(multiplexer_8_out), .sel(or_5_out));
  Register #(.width(52)) R1 (
    .D({multiplexer_5_out_3, multiplexer_5_out_2, multiplexer_5_out}), .en(demultiplexer_2_out4),
    .clk(clock_1_out), .Q(R1_q), .clr(and_3_out));
  Register #(.width(60)) IR (
    .D(multiplexer_6_out), .en(and_5_out), .Q({IR_q_3, IR_q[7], IR_q_2, IR_q[3:0]}), .clk(clock_1_out),
    .clr(and_3_out));
  and and_5 (and_5_out, demultiplexer_3_out0, comparator_2_eq);
  or or_6 (or_6_out, d_ff_5_q, and_3_out);
  D_Flip_Flop d_ff_5 (.clk(clock_1_out), .D(or_6_out), .Q(d_ff_5_q), .reset(and_6_out));  // open: Qn, preset
  and and_6 (and_6_out, d_ff_5_q, d_ff_4_q);
  Comparator #(.mode("unsigned"), .width(29)) comparator_2 (
    .a(multiplexer_7_out), .b(multiplexer_8_out), .eq(comparator_2_eq));  // open: gt, lt
  Register #(.width(52)) R2 (
    .D({multiplexer_5_out_3, multiplexer_5_out_2, multiplexer_5_out}), .en(demultiplexer_2_out5),
    .clk(clock_1_out), .Q(R2_q), .clr(and_3_out));
  Register #(.width(52)) R3 (
    .D({multiplexer_5_out_3, multiplexer_5_out_2, multiplexer_5_out}), .en(demultiplexer_2_out6),
    .clk(clock_1_out), .Q(R3_q), .clr(and_3_out));
  Demultiplexer demultiplexer_3 (
    .out0(demultiplexer_3_out0), .out1(demultiplexer_3_out1), .in(and_7_out), .sel(counter_3_q));
  D_Flip_Flop d_ff_6 (.clk(clock_1_out), .D(d_ff_5_q), .Q(d_ff_6_q), .reset(or_7_out));  // open: Qn, preset
  Counter #(.max('h1), .width(1)) counter_3 (
    .count(and_9_out), .Q(counter_3_q), .up(1'b1), .clk(clock_1_out), .clr(or_7_out));  // open: load, D, carry
  or or_7 (or_7_out, d_ff_8_q, and_3_out);
  Register #(.width(14)) ADR_CACHE (
    .D(multiplexer_5_out), .en(demultiplexer_2_out7), .Q(ADR_CACHE_q), .clk(clock_1_out), .clr(and_3_out));
  and and_7 (and_7_out, 1'b1, and_9_out);
  not not_6 (not_6_out, d_ff_6_q);
  and and_8 (and_8_out, not_6_out, d_ff_5_q);
  not not_7 (not_7_out, d_ff_5_q);
  or or_8 (or_8_out, d_ff_8_q, demultiplexer_2_out12);
  or or_9 (or_9_out, and_3_out, d_ff_7_q);
  D_Flip_Flop d_ff_7 (.clk(clock_1_out), .D(and_1_out), .Q(d_ff_7_q), .reset(and_3_out));  // open: Qn, preset
  RAM #(.addrWidth(14), .clearpin("true"), .dataWidth(52)) CACHE_L2 (
    .addr(ADR_CACHE_q), .we(ram_load_read_controller_3_store), .oe(ram_load_read_controller_3_load),
    .clk(clock_1_out), .din({multiplexer_5_out_3, multiplexer_5_out_2, multiplexer_5_out}),
    .dout(CACHE_L2_dout), .clr(and_3_out));
  RAM_LOAD_READ_CONTROLLER ram_load_read_controller_3 (
    .STORE_SIGNAL(demultiplexer_2_out8), .STORE(ram_load_read_controller_3_store),
    .LOAD(ram_load_read_controller_3_load));
  and and_9 (and_9_out, not_8_out, not_7_out);
  not not_8 (not_8_out, d_ff_8_q);
  D_Flip_Flop d_ff_8 (.clk(clock_1_out), .D(or_8_out), .Q(d_ff_8_q), .reset(or_9_out));  // open: Qn, preset
  Register #(.width(48)) GPU_INST (
    .D({multiplexer_5_out_2, multiplexer_5_out}), .en(demultiplexer_2_out9), .Q(GPU_INST_q),
    .clk(clock_1_out), .clr(and_3_out));
  and and_10 (and_10_out, comparator_3_lt, 1'b0);
  Counter #(.max('h3f), .width(6)) counter_4 (
    .count(and_10_out), .Q(counter_4_q), .up(1'b1), .clk(clock_1_out), .clr(or_10_out));  // open: load, D, carry
  or or_10 (or_10_out, and_3_out, demultiplexer_2_out9);
  ROM #(.addrWidth(24), .dataWidth(24)) Resources (.addr(adder_2_out), .data(Resources_data));
  Adder #(.width(24)) adder_2 (.a(bit_extender_5_out), .b(GPU_INST_q[47:24]), .out(adder_2_out));  // open: cin, cout
  assign bit_extender_5_out = {{18{1'b0}}, counter_4_q};  // Bit_Extender bit_extender_5
  Counter #(.max('hffff), .width(16)) SCREEN (
    .Q(SCREEN_q), .up(1'b1), .clk(clock_1_out), .clr(and_3_out));  // open: load, D, count, carry
  not not_9 (not_9_out, d_ff_9_q);
  D_Flip_Flop d_ff_9 (.clk(clock_1_out), .D(comparator_3_eq), .Q(d_ff_9_q), .reset(and_3_out));  // open: Qn, preset
  Comparator #(.mode("unsigned"), .width(6)) comparator_3 (
    .a(counter_4_q), .b({6{1'b1}}), .eq(comparator_3_eq), .lt(comparator_3_lt));  // open: gt
  Divider #(.width(6)) divider_2 (
    .a(counter_4_q), .b({6{1'b1}}), .out(divider_2_out), .rem(divider_2_rem));  // open: upper
  and and_11 (and_11_out, comparator_3_eq, not_9_out);
  or or_11 (or_11_out, and_3_out, and_12_out);
  assign out_1 = {{2{1'b0}}, divider_2_out};  // Bit_Extender bit_extender_6
  assign out_2 = {{2{1'b0}}, divider_2_rem};  // Bit_Extender bit_extender_7
  S_R_Flip_Flop s_r_ff_1 (.S(and_11_out), .clk(clock_1_out), .Q(s_r_ff_1_q), .reset(or_11_out));  // open: R, Qn, preset
  Multiplexer #(.width(16)) multiplexer_9 (
    .in0(SCREEN_q), .in1(adder_3_out), .out(multiplexer_9_out), .sel(BufferInScreen_q));
  Adder #(.width(16)) adder_3 (.a(GPU_INST_q[17:2]), .b({out_2, out_1}), .out(adder_3_out));  // open: cin, cout
  RAM_LOAD_READ_CONTROLLER ram_load_read_controller_4 (
    .STORE_SIGNAL(BufferInScreen_q), .STORE(ram_load_read_controller_4_store),
    .LOAD(ram_load_read_controller_4_load));
  Demultiplexer #(.width(24)) demultiplexer_4 (
    .out0(demultiplexer_4_out0), .out1(demultiplexer_4_out1), .in(Resources_data), .sel(not_10_out));
  not not_10 (not_10_out, BufferInScreen_q);
  Multiplexer #(.width(16)) multiplexer_10 (
    .in0(SCREEN_q), .in1(adder_3_out), .out(multiplexer_10_out), .sel(not_10_out));
  RAM_LOAD_READ_CONTROLLER ram_load_read_controller_5 (
    .STORE_SIGNAL(not_10_out), .STORE(ram_load_read_controller_5_store),
    .LOAD(ram_load_read_controller_5_load));
  // RGB_Video #(.cursor("No Cursor"), .height(256), .width(256)) rgb_video_1: pin names not known; wires that end beside it: and_3_out, clock_1_out, 1'b1, SCREEN_q[7:0], SCREEN_q[15:8], rgb_video_1_p6
  Comparator #(.mode("unsigned"), .width(16)) comparator_4 (
    .a(SCREEN_q), .b({16{1'b1}}), .eq(comparator_4_eq));  // open: gt, lt
  RAM #(.addrWidth(16), .clearpin("true"), .dataWidth(24)) FrameBuffer0 (
    .addr(multiplexer_9_out), .we(ram_load_read_controller_4_store), .oe(ram_load_read_controller_4_load),
    .clk(clock_1_out), .din(demultiplexer_4_out0), .dout(FrameBuffer0_dout), .clr(and_3_out));
  RAM #(.addrWidth(16), .clearpin("true"), .dataWidth(24)) FrameBuffer1 (
    .addr(multiplexer_10_out), .we(ram_load_read_controller_5_store), .oe(ram_load_read_controller_5_load),
    .clk(clock_1_out), .din(demultiplexer_4_out1), .dout(FrameBuffer1_dout), .clr(and_3_out));
  and and_12 (and_12_out, comparator_4_eq, s_r_ff_1_q);
  Counter #(.max('h1), .width(1)) BufferInScreen (
    .count(and_12_out), .Q(BufferInScreen_q), .up(1'b1), .clk(clock_1_out), .clr(and_3_out));  // open: load, D, carry
  Multiplexer #(.width(24)) multiplexer_11 (
    .in0(FrameBuffer0_dout), .in1(FrameBuffer1_dout), .out(rgb_video_1_p6), .sel(BufferInScreen_q));

  // Notes on the sheet:
  //   contents of Resources (hex, n*v repeats v):
  //   73*0 5*7cff 0 0 7cff 5*0 7cff 0 7cff 5*0 7cff 0 7cff 5*0 7cff 0 7*7cff 0 7cff 5*0 7cff 0 7cff 5*0
  //   7cff 9*0 6*7cff 0 0 7cff 5*0 7cff 0 7cff 5*0 7cff 0 6*7cff 0 0 7cff 5*0 7cff 0 7cff 5*0 7cff 0
  //   6*7cff 11*0 5*ffffff 0 0 ffffff 5*0 ffffff 0 ffffff 7*0 ffffff 7*0 ffffff 7*0 ffffff 5*0 ffffff 0 0
  //   5*ffffff 10*0 5*ffffff 0 0 0 ffffff 4*0 ffffff 0 0 ffffff 5*0 ffffff 0 ffffff 5*0 ffffff 0 ffffff
  //   5*0 ffffff 0 ffffff 4*0 ffffff 0 0 5*ffffff 11*0 7*ffffff 0 ffffff 7*0 ffffff 7*0 7*ffffff 0 ffffff
  //   7*0 ffffff 7*0 7*ffffff 9*0 7*ffffff 0 ffffff 7*0 ffffff 7*0 7*ffffff 0 ffffff 7*0 ffffff 7*0 ffffff
  //   17*0 4*ffffff 0 0 0 ffffff 4*0 ffffff 0 ffffff 7*0 ffffff 0 0 4*ffffff 0 ffffff 5*0 ffffff 0 0
  //   ffffff 4*0 ffffff 0 0 0 4*ffffff 10*0 ffffff 5*0 ffffff 0 ffffff 5*0 ffffff 0 ffffff 5*0 ffffff 0
  //   7*ffffff 0 ffffff 5*0 ffffff 0 ffffff 5*0 ffffff 0 ffffff 5*0 ffffff 9*0 7*ffffff 4*0 ffffff 7*0
  //   ffffff 7*0 ffffff 7*0 ffffff 7*0 ffffff 4*0 7*ffffff 14*0 ffffff 7*0 ffffff 7*0 ffffff 7*0 ffffff
  //   7*0 ffffff 0 0 0 ffffff 0 0 0 ffffff 4*0 ffffff ffffff ffffff 11*0 ffffff 5*0 ffffff 0 ffffff 5*0
  //   ffffff 0 ffffff 4*0 ffffff 0 0 5*ffffff 0 0 0 ffffff 4*0 ffffff 0 0 ffffff 5*0 ffffff 0 ffffff 5*0
  //   ffffff 10*0 ffffff 7*0 ffffff 7*0 ffffff 7*0 ffffff 7*0 ffffff 7*0 ffffff 7*0 6*ffffff 9*0 ffffff
  //   ffffff 0 0 0 ffffff ffffff 0 ffffff 0 ffffff 0 ffffff 0 ffffff 0 ffffff 0 0 ffffff 0 0 ffffff 0
  //   ffffff 5*0 ffffff 0 ffffff 5*0 ffffff 0 ffffff 5*0 ffffff 0 ffffff 5*0 ffffff 9*0 ffffff 5*0 ffffff
  //   0 ffffff ffffff 4*0 ffffff 0 ffffff 0 ffffff 0 0 0 ffffff 0 ffffff 0 0 ffffff 0 0 ffffff 0 ffffff 0
  //   0 0 ffffff 0 ffffff 0 ffffff 4*0 ffffff ffffff 0 ffffff 5*0 ffffff 9*0 7*ffffff 9*0 ffffff ffffff
  //   4*0 ffffff 0 ffffff 0 ffffff 0 0 0 ffffff 0 ffffff 0 0 ffffff 0 0 ffffff 0 ffffff 0 0 0 ffffff 0
  //   ffffff 0 ffffff 4*0 ffffff ffffff 10*0 5*ffffff 0 0 ffffff 5*0 ffffff 0 ffffff 5*0 ffffff 0 ffffff
  //   5*0 ffffff 0 ffffff 5*0 ffffff 0 ffffff 5*0 ffffff 0 0 5*ffffff 10*0 6*ffffff 0 0 ffffff 5*0 ffffff
  //   0 ffffff 5*0 ffffff 0 ffffff 5*0 ffffff 0 6*ffffff 0 0 ffffff 7*0 ffffff 16*0 5*ffffff 0 0 ffffff
  //   5*0 ffffff 0 ffffff 5*0 ffffff 0 ffffff 5*0 ffffff 0 ffffff 5*0 ffffff 0 ffffff 4*0 ffffff 0 0 0
  //   4*ffffff 0 ffffff 9*0 6*ffffff 0 0 ffffff 5*0 ffffff 0 ffffff 5*0 ffffff 0 ffffff 5*0 ffffff 0
  //   6*ffffff 0 0 ffffff 5*0 ffffff 0 ffffff 5*0 ffffff 10*0 5*ffffff 0 0 ffffff 5*0 ffffff 0 ffffff 8*0
  //   5*ffffff 8*0 ffffff 0 ffffff 5*0 ffffff 0 0 5*ffffff 10*0 7*ffffff 4*0 ffffff 7*0 ffffff 7*0 ffffff
  //   7*0 ffffff 7*0 ffffff 7*0 ffffff 12*0 ffffff 5*0 ffffff 0 ffffff 5*0 ffffff 0 ffffff 5*0 ffffff 0
  //   ffffff 5*0 ffffff 0 ffffff 5*0 ffffff 0 ffffff 5*0 ffffff 0 0 5*ffffff 10*0 ffffff 5*0 ffffff 0
  //   ffffff 5*0 ffffff 0 0 ffffff 0 0 0 ffffff 0 0 0 ffffff 0 0 0 ffffff 4*0 ffffff 0 ffffff 5*0 ffffff 0
  //   ffffff 6*0 ffffff 12*0 ffffff 5*0 ffffff 0 ffffff 5*0 ffffff 0 ffffff 5*0 ffffff 0 ffffff 5*0 ffffff
  //   0 0 ffffff 0 ffffff 0 ffffff 0 0 0 ffffff 0 ffffff 0 ffffff 4*0 ffffff 0 ffffff 11*0 ffffff 5*0
  //   ffffff 0 ffffff 5*0 ffffff 0 0 ffffff 0 0 0 ffffff 4*0 ffffff ffffff ffffff 4*0 ffffff 0 0 0 ffffff
  //   0 0 ffffff 5*0 ffffff 0 ffffff 5*0 ffffff 9*0 ffffff 5*0 ffffff 0 ffffff 5*0 ffffff 0 ffffff 5*0
  //   ffffff 0 0 6*ffffff 7*0 ffffff 0 ffffff 5*0 ffffff 0 0 5*ffffff 10*0 7*ffffff 7*0 ffffff 6*0 ffffff
  //   4*0 ffffff ffffff ffffff 4*0 ffffff 6*0 ffffff 7*0 7*ffffff 26*0 ffffff ffffff ffffff 8*0 ffffff 4*0
  //   4*ffffff 0 0 0 ffffff 0 0 0 ffffff 4*0 ffffff ffffff ffffff 12*0 ffffff 7*0 ffffff 7*0 ffffff 7*0
  //   4*ffffff 4*0 ffffff 0 0 0 ffffff 0 0 0 ffffff 0 0 0 ffffff 0 0 0 4*ffffff 29*0 ffffff ffffff ffffff
  //   4*0 ffffff 0 0 0 ffffff 0 0 0 ffffff 7*0 ffffff 0 0 0 ffffff 4*0 ffffff ffffff ffffff 16*0 ffffff
  //   7*0 ffffff 7*0 ffffff 4*0 4*ffffff 0 0 0 ffffff 0 0 0 ffffff 0 0 0 ffffff 0 0 0 ffffff 4*0 4*ffffff
  //   28*0 ffffff ffffff ffffff 4*0 ffffff 0 0 0 ffffff 0 0 0 5*ffffff 0 0 0 ffffff 8*0 4*ffffff 12*0
  //   ffffff ffffff ffffff 4*0 ffffff 0 0 0 ffffff 0 0 0 ffffff 7*0 ffffff 7*0 4*ffffff 4*0 ffffff 7*0
  //   ffffff 16*0 ffffff ffffff ffffff 4*0 ffffff 0 0 0 ffffff 0 0 0 fff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
endmodule

module RAM_LOAD_READ_CONTROLLER (
  input  STORE_SIGNAL,
  output STORE,
  output LOAD
);

  Demultiplexer demultiplexer_1 (.out0(LOAD), .out1(STORE), .in(1'b1), .sel(STORE_SIGNAL));
endmodule

module DELAY_CIRC (
  input  in_1
);

  wire and_1_out, clock_1_out, not_1_out, register_1_q;

  Register #(.width(1)) register_1 (.D(not_1_out), .en(1'b1), .clk(clock_1_out), .Q(register_1_q), .clr(in_1));
  Clock clock_1 (.out(clock_1_out));
  not not_1 (not_1_out, register_1_q);
  and and_1 (and_1_out, register_1_q, 1'b1);
endmodule
